// Digital circuit RAM.dig as structural Verilog
module RAM (
  input  [3:0] A_in,
  input  RO,
  input  PROG,
  input  CLK,
  input  RI,
  input  Trig_Prog,
  input  [7:0] D_Prog,
  input  [3:0] A_PROG,
  output [7:0] Bus
);

  wire _7404_1_pin1, _7404_1_pin3, _7404_1_pin5, _7404_1_pin9, _7404_2_pin1, _7404_2_pin3, _7404_2_pin5,
       _7404_2_pin9, _74157_1_pin12, _74157_1_pin13, _74189_1_pin4, _74189_1_pin6, _74189_1_pin10,
       _74189_1_pin12, _74189_2_pin4, _74189_2_pin6, _74189_2_pin10, _74189_2_pin12, _74245_1_pin2,
       _74245_1_pin3, _74245_1_pin4, _74245_1_pin5, _74245_1_pin6, _74245_1_pin7, _74245_1_pin8,
       _74245_1_pin9, _74245_1_pin11, _74245_1_pin12, _74245_1_pin13, _74245_1_pin14, _74245_1_pin15,
       _74245_1_pin16, _74245_1_pin17, _74245_1_pin18, not_1_out, not_2_out, not_3_out, or_1_out;
  wire [3:0] _74189_1_pin1;
  wire [7:0] driver_1_out;

  _74157 _74157_1 (
    .pin1(PROG), .pin2(1'b0), .pin3(1'b0), .pin5(1'b0), .pin6(1'b0), .pin8(1'b0), .pin10(1'b0), .pin11(1'b0),
    .pin12(_74157_1_pin12), .pin13(_74157_1_pin13), .pin14(Trig_Prog), .pin15(1'b0), .pin16(1'b1));  // open: pin4, pin7, pin9
  not not_1 (not_1_out, PROG);
  or or_1 (or_1_out, RI, not_1_out);
  _7400 _7400_1 (
    .pin1(or_1_out), .pin2(CLK), .pin3(_74157_1_pin13), .pin4(1'b0), .pin5(1'b0), .pin7(1'b0), .pin9(1'b1),
    .pin10(1'b1), .pin12(1'b1), .pin13(1'b1), .pin14(1'b1));  // open: pin6, pin8, pin11
  _74245 _74245_1 (
    .pin1(1'b1), .pin2(_74245_1_pin2), .pin3(_74245_1_pin3), .pin4(_74245_1_pin4), .pin5(_74245_1_pin5),
    .pin6(_74245_1_pin6), .pin7(_74245_1_pin7), .pin8(_74245_1_pin8), .pin9(_74245_1_pin9), .pin10(1'b0),
    .pin11(_74245_1_pin11), .pin12(_74245_1_pin12), .pin13(_74245_1_pin13), .pin14(_74245_1_pin14),
    .pin15(_74245_1_pin15), .pin16(_74245_1_pin16), .pin17(_74245_1_pin17), .pin18(_74245_1_pin18),
    .pin19(RO), .pin20(1'b1));
  _7404 _7404_1 (
    .pin1(_7404_1_pin1), .pin2(_74245_1_pin2), .pin3(_7404_1_pin3), .pin4(_74245_1_pin3),
    .pin5(_7404_1_pin5), .pin6(_74245_1_pin4), .pin7(1'b0), .pin8(_74245_1_pin5), .pin9(_7404_1_pin9),
    .pin11(1'b1), .pin13(1'b1), .pin14(1'b1));  // open: pin10, pin12
  _74189 _74189_1 (
    .pin1(_74189_1_pin1[0]), .pin2(1'b0), .pin3(_74157_1_pin12), .pin4(_74189_1_pin4), .pin5(_7404_1_pin1),
    .pin6(_74189_1_pin6), .pin7(_7404_1_pin3), .pin8(1'b0), .pin9(_7404_1_pin5), .pin10(_74189_1_pin10),
    .pin11(_7404_1_pin9), .pin12(_74189_1_pin12), .pin13(_74189_1_pin1[3]), .pin14(_74189_1_pin1[2]),
    .pin15(_74189_1_pin1[1]), .pin16(1'b1));
  _74157 _74157_2 (
    .pin1(PROG), .pin2(driver_1_out[7]), .pin3(_74245_1_pin18), .pin4(_74189_1_pin4), .pin5(driver_1_out[6]),
    .pin6(_74245_1_pin17), .pin7(_74189_1_pin6), .pin8(1'b0), .pin9(_74189_1_pin10), .pin10(_74245_1_pin16),
    .pin11(driver_1_out[5]), .pin12(_74189_1_pin12), .pin13(_74245_1_pin15), .pin14(driver_1_out[4]),
    .pin15(1'b0), .pin16(1'b1));
  LED led_1 (.in(_74245_1_pin2));
  LED led_2 (.in(_74245_1_pin3));
  LED led_3 (.in(_74245_1_pin4));
  LED led_4 (.in(_74245_1_pin5));
  LED led_5 (.in(_74245_1_pin6));
  LED led_6 (.in(_74245_1_pin7));
  LED led_7 (.in(_74245_1_pin8));
  LED led_8 (.in(_74245_1_pin9));
  assign driver_1_out = not_2_out ? D_Prog : 8'bz;  // Driver driver_1
  _7404 _7404_2 (
    .pin1(_7404_2_pin1), .pin2(_74245_1_pin6), .pin3(_7404_2_pin3), .pin4(_74245_1_pin7),
    .pin5(_7404_2_pin5), .pin6(_74245_1_pin8), .pin7(1'b0), .pin8(_74245_1_pin9), .pin9(_7404_2_pin9),
    .pin11(1'b1), .pin13(1'b1), .pin14(1'b1));  // open: pin10, pin12
  _74189 _74189_2 (
    .pin1(_74189_1_pin1[0]), .pin2(1'b0), .pin3(_74157_1_pin12), .pin4(_74189_2_pin4), .pin5(_7404_2_pin1),
    .pin6(_74189_2_pin6), .pin7(_7404_2_pin3), .pin8(1'b0), .pin9(_7404_2_pin5), .pin10(_74189_2_pin10),
    .pin11(_7404_2_pin9), .pin12(_74189_2_pin12), .pin13(_74189_1_pin1[3]), .pin14(_74189_1_pin1[2]),
    .pin15(_74189_1_pin1[1]), .pin16(1'b1));
  _74157 _74157_3 (
    .pin1(PROG), .pin2(driver_1_out[3]), .pin3(_74245_1_pin14), .pin4(_74189_2_pin4), .pin5(driver_1_out[2]),
    .pin6(_74245_1_pin13), .pin7(_74189_2_pin6), .pin8(1'b0), .pin9(_74189_2_pin10), .pin10(_74245_1_pin12),
    .pin11(driver_1_out[1]), .pin12(_74189_2_pin12), .pin13(_74245_1_pin11), .pin14(driver_1_out[0]),
    .pin15(1'b0), .pin16(1'b1));
  not not_2 (not_2_out, PROG);
  BusSplitter #(.Bits(8)) bussplitter_1 (
    .D(Bus), .OE(RO), .D0(_74245_1_pin11), .D1(_74245_1_pin12), .D2(_74245_1_pin13), .D3(_74245_1_pin14),
    .D4(_74245_1_pin15), .D5(_74245_1_pin16), .D6(_74245_1_pin17), .D7(_74245_1_pin18));
  assign _74189_1_pin1 = PROG ? A_in : 4'bz;  // Driver driver_2
  assign _74189_1_pin1 = not_3_out ? A_PROG : 4'bz;  // Driver driver_3
  not not_3 (not_3_out, PROG);

  // Notes on the sheet:
  //   RO: default 1
  //   PROG: default 1
  //   Trig_Prog: default 1
endmodule
