// Digital circuit SAP-1.dig as structural Verilog
module SAP_1 (
  input  clk,
  input  clk_2
);

  wire AI, AO, BI, Burn_out, CE, CF, CLK_t, CLK_t_t, CLR, CLR_t, CO, control_logic_1_rst, EO, FI, HALT, II,
       IO, J, MI, not_1_out, OI, PROG_EN_out, RI, RO, STEP_2_out, STEP_out, SU, ZF;
  wire [3:0] dipswitch_1_out, output_register_1_sel_digit, program_counter_1_leds, register_instruction_1_p6,
       register_mad_1_a_out;
  wire [4:0] control_logic_1_step_ucode;
  wire [7:0] dipswitch_5_out, output_register_1_display_out, program_counter_1_bus, register_a_1_a_out,
       register_b_1_b_out;

  Button STEP (.out(STEP_out));
  LED led_1 (.in(register_a_1_a_out[7]));
  LED led_2 (.in(register_b_1_b_out[7]));
  LED led_3 (.in(register_b_1_b_out[6]));
  LED led_4 (.in(program_counter_1_leds[2]));
  LED led_5 (.in(program_counter_1_leds[3]));
  program_counter program_counter_1 (
    .CO(CO), .CLK(CLK_t_t), .CLR(CLR_t), .CE(CE), .J(J), .LEDs(program_counter_1_leds),
    .Bus(program_counter_1_bus));
  clock_module clock_module_1 (
    .HLT(HALT), .STEP_EN(STEP_2_out), .STEP_in(STEP_out), .CLK_in(clk), .CLK(CLK_t_t), .CLK_2(CLK_t));
  DipSwitch STEP_2 (.out(STEP_2_out));
  register_A register_a_1 (
    .CLK(CLK_t_t), .AO(AO), .AI(AI), .CLR(CLR_t), .BUS(program_counter_1_bus[0]), .A_out(register_a_1_a_out));
  LED led_6 (.in(register_a_1_a_out[6]));
  LED led_7 (.in(register_a_1_a_out[5]));
  register_B register_b_1 (
    .CLK(CLK_t_t), .BI(BI), .CLR(CLR_t), .BUS(program_counter_1_bus[0]), .B_out(register_b_1_b_out));
  LED led_8 (.in(register_b_1_b_out[5]));
  LED led_9 (.in(register_b_1_b_out[4]));
  // register_Instruction register_instruction_1: pin names not known; wires that end beside it: CLK_t_t, IO, II, CLR_t, program_counter_1_bus, register_instruction_1_p6
  LED led_10 (.in(program_counter_1_leds[0]));
  LED led_11 (.in(program_counter_1_leds[1]));
  LED led_12 (.in(register_a_1_a_out[4]));
  LED led_13 (.in(register_a_1_a_out[3]));
  LED led_14 (.in(register_b_1_b_out[3]));
  LED led_15 (.in(register_b_1_b_out[2]));
  LED led_16 (.in(register_instruction_1_p6[3]));
  LED led_17 (.in(register_instruction_1_p6[2]));
  LED led_18 (.in(CLK_t_t));
  LED led_19 (.in(register_a_1_a_out[2]));
  LED led_20 (.in(register_a_1_a_out[1]));
  LED led_21 (.in(register_b_1_b_out[1]));
  LED led_22 (.in(register_b_1_b_out[0]));
  LED led_23 (.in(register_instruction_1_p6[1]));
  LED led_24 (.in(register_instruction_1_p6[0]));
  LED led_25 (.in(register_a_1_a_out[0]));
  control_logic control_logic_1 (
    .CLK(CLK_t), .CF(CF), .ZF(ZF), .Step_ucode(control_logic_1_step_ucode), .IR(register_instruction_1_p6),
    .RST(control_logic_1_rst), .CLR(CLR_t), .HLT(HALT), .MI(MI), .RI(RI), .RO(RO), .IO(IO), .II(II), .AI(AI),
    .AO(AO), .CLR_2(CLR), .EO(EO), .SU(SU), .BI(BI), .OI(OI), .CE(CE), .CO(CO), .J(J), .FI(FI));
  LED T_1 (.in(control_logic_1_step_ucode[0]));
  Button button_1 (.out(control_logic_1_rst));
  LED T_2 (.in(control_logic_1_step_ucode[1]));
  LED T_3 (.in(control_logic_1_step_ucode[2]));
  // ALU alu_1: pin names not known; wires that end beside it: CLK_t_t, EO, register_b_1_b_out, SU, CLR_t, FI, register_a_1_a_out, program_counter_1_bus, CF, ZF
  LED T_4 (.in(control_logic_1_step_ucode[3]));
  LED T_5 (.in(control_logic_1_step_ucode[4]));
  not not_1 (not_1_out, PROG_EN_out);
  DipSwitch PROG_EN (.out(PROG_EN_out));
  LED u_CF (.in(CF));
  LED u_ZF (.in(ZF));
  Button #(.activeLow("true")) Burn (.out(Burn_out));
  DipSwitch dipswitch_1 (.out(dipswitch_1_out[3]));
  DipSwitch dipswitch_2 (.out(dipswitch_1_out[2]));
  DipSwitch dipswitch_3 (.out(dipswitch_1_out[1]));
  DipSwitch dipswitch_4 (.out(dipswitch_1_out[0]));
  register_MAD register_mad_1 (
    .MI(MI), .CLK(CLK_t_t), .CLR(CLR_t), .PROG_in(not_1_out), .Bus_in(program_counter_1_bus),
    .A_out(register_mad_1_a_out));  // open: PROG_out
  RAM ram_1 (
    .A_in(register_mad_1_a_out), .RO(RO), .PROG(not_1_out), .CLK(CLK_t_t), .RI(RI), .Trig_Prog(Burn_out),
    .D_Prog(dipswitch_5_out), .A_PROG(dipswitch_1_out), .Bus(program_counter_1_bus));
  DipSwitch dipswitch_5 (.out(dipswitch_5_out[7]));
  DipSwitch dipswitch_6 (.out(dipswitch_5_out[6]));
  DipSwitch dipswitch_7 (.out(dipswitch_5_out[5]));
  DipSwitch dipswitch_8 (.out(dipswitch_5_out[4]));
  DipSwitch dipswitch_9 (.out(dipswitch_5_out[3]));
  LED led_26 (.in(register_mad_1_a_out[3]));
  DipSwitch dipswitch_10 (.out(dipswitch_5_out[2]));
  DipSwitch dipswitch_11 (.out(dipswitch_5_out[1]));
  DipSwitch dipswitch_12 (.out(dipswitch_5_out[0]));
  LED led_27 (.in(register_mad_1_a_out[2]));
  LED led_28 (.in(register_mad_1_a_out[1]));
  LED led_29 (.in(register_mad_1_a_out[0]));
  output_register output_register_1 (
    .Refresh_display(clk_2), .OI(OI), .CLK(CLK_t_t), .CLR(CLR_t), .Bus(program_counter_1_bus),
    .SEL_digit(output_register_1_sel_digit), .Display_out(output_register_1_display_out));
  Seven_Seg #(.commonCathode("true")) seven_seg_1 (
    .a(output_register_1_display_out[0]), .b(output_register_1_display_out[1]),
    .c(output_register_1_display_out[2]), .d(output_register_1_display_out[3]),
    .e(output_register_1_display_out[4]), .f(output_register_1_display_out[5]),
    .g(output_register_1_display_out[6]), .dp(output_register_1_display_out[7]),
    .common(output_register_1_sel_digit[3]));
  Seven_Seg #(.commonCathode("true")) seven_seg_2 (
    .a(output_register_1_display_out[0]), .b(output_register_1_display_out[1]),
    .c(output_register_1_display_out[2]), .d(output_register_1_display_out[3]),
    .e(output_register_1_display_out[4]), .f(output_register_1_display_out[5]),
    .g(output_register_1_display_out[6]), .dp(output_register_1_display_out[7]),
    .common(output_register_1_sel_digit[2]));
  Seven_Seg #(.commonCathode("true")) seven_seg_3 (
    .a(output_register_1_display_out[0]), .b(output_register_1_display_out[1]),
    .c(output_register_1_display_out[2]), .d(output_register_1_display_out[3]),
    .e(output_register_1_display_out[4]), .f(output_register_1_display_out[5]),
    .g(output_register_1_display_out[6]), .dp(output_register_1_display_out[7]),
    .common(output_register_1_sel_digit[1]));
  Seven_Seg #(.commonCathode("true")) seven_seg_4 (
    .a(output_register_1_display_out[0]), .b(output_register_1_display_out[1]),
    .c(output_register_1_display_out[2]), .d(output_register_1_display_out[3]),
    .e(output_register_1_display_out[4]), .f(output_register_1_display_out[5]),
    .g(output_register_1_display_out[6]), .dp(output_register_1_display_out[7]),
    .common(output_register_1_sel_digit[0]));
  // Pins of 1 and 8 bits meet at program_counter_1_bus

  // Notes on the sheet:
  //   clk_2: Hz: 100
  //   Clock
  //   A Register
  //   B Register
  //   Instruction Register
  //   Program Counter
  //   Logic Controller
  //   ALU
  //   RESET
  //   Memory Address Register
  //   RAM
  //   Addr
  //   Data
  //   Output Register
endmodule
